// Logisim project Simulação logisim dum FLIP FLOP D  (não funciona correctamente).circ as structural Verilog: 1 circuit, main circuit main
module main (
  input  in_1
);

  wire clock_1_out, d_ff_1_q, d_ff_1_qn;

  Clock clock_1 (.out(clock_1_out));
  D_Flip_Flop d_ff_1 (
    .clk(in_1), .D(clock_1_out), .Q(d_ff_1_q), .Qn(d_ff_1_qn), .preset(1'b0), .reset(1'b0));  // open: en
  LED led_1 (.in(d_ff_1_q));
  LED led_2 (.in(d_ff_1_qn));
endmodule
