// Logisim project Simulação logisim dum Flip Flop t apartir dum D.circ as structural Verilog: 1 circuit, main circuit main
module main (
  input  in_1,
  output out_2
);

  wire nor_1_out;

  nor nor_1 (nor_1_out, in_1, out_2);
  D_Flip_Flop d_ff_1 (.D(nor_1_out), .Q(out_2));  // open: clk, Qn, preset, en, reset

  // Notes on the sheet:
  //   Flip-Flop D
endmodule
