// Logisim project Simulação logisim dum circuito debounce.circ as structural Verilog: 1 circuit, main circuit main
module main (
);

  wire nand_1_out, nand_2_out, pull_resistor_1_node, pull_resistor_2_node;

  Pull_Resistor #(.pull(1)) pull_resistor_1 (.node(pull_resistor_1_node));
  Pull_Resistor #(.pull(1)) pull_resistor_2 (.node(pull_resistor_2_node));
  nand nand_1 (nand_1_out, pull_resistor_1_node, nand_2_out);
  nand nand_2 (nand_2_out, nand_1_out, pull_resistor_2_node);
  LED led_1 (.in(nand_1_out));
  LED led_2 (.in(nand_2_out));
endmodule
